// Logisim project Project-Combinationals.circ as structural Verilog: 6 circuits, main circuit main
module main (
);

  wire A_2_out, a_3_out, A_q, A_qn, B_2_out, b_3_out, B_q, B_qn, C_2_out, c_3_out, C_q, C_qn, clock_1_out,
       d_out, e_out, f_out, g_out, nand_1_out, nand_2_out, nand_3_out, nand_4_out, nand_5_out, nand_6_out,
       nand_7_out, nand_8_out, nand_9_out, nand_10_out, nand_11_out, nand_12_out, nand_13_out, nand_14_out,
       nand_15_out, nand_16_out, nand_17_out, nand_18_out, nand_19_out, nand_20_out, nand_21_out,
       nand_22_out, nand_23_out, nand_24_out, nand_25_out, nand_26_out, nand_27_out, nand_28_out,
       nand_29_out, nand_30_out, nand_31_out, nand_32_out, nand_33_out, nand_34_out, nand_35_out,
       nand_36_out, nand_37_out, nand_38_out, nand_39_out, nand_40_out, nand_41_out, nand_42_out,
       nand_43_out, nand_44_out, nand_45_out;

  Clock clock_1 (.out(clock_1_out));
  D_Flip_Flop A (.clk(clock_1_out), .D(nand_6_out), .Q(A_q), .Qn(A_qn));  // open: preset, en, reset
  nand nand_1 (nand_1_out, A_q, C_qn);
  nand nand_2 (nand_2_out, A_q, B_qn);
  nand nand_3 (nand_3_out, A_qn, B_q, C_q);
  nand nand_4 (nand_4_out, B_q, C_qn);
  nand nand_5 (nand_5_out, B_qn, C_q);
  D_Flip_Flop B (.clk(clock_1_out), .D(nand_7_out), .Q(B_q), .Qn(B_qn));  // open: preset, en, reset
  nand nand_6 (nand_6_out, nand_1_out, nand_2_out, nand_3_out);
  nand nand_7 (nand_7_out, nand_4_out, nand_5_out);
  D_Flip_Flop C (.clk(clock_1_out), .D(C_qn), .Q(C_q), .Qn(C_qn));  // open: preset, en, reset
  buf A_2 (A_2_out, A_q);
  buf B_2 (B_2_out, B_q);
  buf C_2 (C_2_out, C_q);
  nand nand_8 (nand_8_out, B_2_out, B_2_out);
  nand nand_9 (nand_9_out, C_2_out, C_2_out);
  nand nand_10 (nand_10_out, A_2_out, A_2_out);
  nand nand_11 (nand_11_out, B_2_out, B_2_out);
  nand nand_12 (nand_12_out, C_2_out, C_2_out);
  nand nand_13 (nand_13_out, A_2_out, A_2_out);
  nand nand_14 (nand_14_out, C_2_out, C_2_out);
  nand nand_15 (nand_15_out, A_2_out, A_2_out);
  nand nand_16 (nand_16_out, C_2_out, C_2_out);
  nand nand_17 (nand_17_out, B_2_out, B_2_out);
  nand nand_18 (nand_18_out, C_2_out, C_2_out);
  nand nand_19 (nand_19_out, B_2_out, B_2_out);
  nand nand_20 (nand_20_out, B_2_out, C_2_out);
  nand nand_21 (nand_21_out, A_2_out, A_2_out);
  nand nand_22 (nand_22_out, A_2_out, A_2_out);
  nand nand_23 (nand_23_out, B_2_out, B_2_out);
  nand nand_24 (nand_24_out, C_2_out, C_2_out);
  nand nand_25 (nand_25_out, B_2_out, B_2_out);
  nand nand_26 (nand_26_out, A_2_out, nand_8_out, C_2_out);
  nand nand_27 (nand_27_out, A_2_out, B_2_out, nand_9_out);
  nand nand_28 (nand_28_out, nand_10_out, nand_11_out);
  nand nand_29 (nand_29_out, B_2_out, nand_12_out);
  nand nand_30 (nand_30_out, nand_13_out, nand_14_out);
  nand nand_31 (nand_31_out, nand_15_out, B_2_out);
  nand nand_32 (nand_32_out, B_2_out, nand_16_out);
  nand nand_33 (nand_33_out, A_2_out, nand_17_out, C_2_out);
  nand nand_34 (nand_34_out, A_2_out, B_2_out, nand_18_out);
  nand nand_35 (nand_35_out, nand_19_out, C_2_out);
  nand nand_36 (nand_36_out, A_2_out, A_2_out);
  nand nand_37 (nand_37_out, nand_20_out, nand_21_out);
  nand nand_38 (nand_38_out, nand_22_out, nand_23_out, nand_24_out);
  nand nand_39 (nand_39_out, A_2_out, nand_25_out, C_2_out);
  nand nand_40 (nand_40_out, nand_26_out, nand_27_out);
  nand nand_41 (nand_41_out, nand_28_out, nand_29_out);
  nand nand_42 (nand_42_out, nand_30_out, nand_31_out, nand_32_out);
  nand nand_43 (nand_43_out, nand_33_out, nand_34_out);
  nand nand_44 (nand_44_out, nand_35_out, nand_36_out);
  nand f (f_out, nand_37_out, nand_37_out);
  nand nand_45 (nand_45_out, nand_38_out, nand_39_out);
  nand a_3 (a_3_out, nand_40_out, nand_40_out);
  nand b_3 (b_3_out, nand_41_out, nand_41_out);
  nand c_3 (c_3_out, nand_42_out, nand_42_out);
  nand d (d_out, nand_43_out, nand_43_out);
  nand e (e_out, nand_44_out, nand_44_out);
  nand g (g_out, nand_45_out, nand_45_out);
  _7_Segment_Display u_7_segment_display_1 (
    .g(g_out), .f(f_out), .a(a_3_out), .b(b_3_out), .e(e_out), .d(d_out), .c(c_3_out));  // open: dp
endmodule

// Decoder
module BCD27 (
  input  A,
  input  B,
  input  C,
  output a_2,
  output b_2,
  output c_2,
  output d,
  output e,
  output f,
  output g
);

  wire nand_1_out, nand_2_out, nand_3_out, nand_4_out, nand_5_out, nand_6_out, nand_7_out, nand_8_out,
       nand_9_out, nand_10_out, nand_11_out, nand_12_out, nand_13_out, nand_14_out, nand_15_out, nand_16_out,
       nand_17_out, nand_18_out, nand_19_out, nand_20_out, nand_21_out, nand_22_out, nand_23_out,
       nand_24_out, nand_25_out, nand_26_out, nand_27_out, nand_28_out, nand_29_out, nand_30_out,
       nand_31_out, nand_32_out, nand_33_out, nand_34_out, nand_35_out, nand_36_out, nand_37_out, nand_39_out;

  nand nand_1 (nand_1_out, B, B);
  nand nand_2 (nand_2_out, C, C);
  nand nand_3 (nand_3_out, A, A);
  nand nand_4 (nand_4_out, B, B);
  nand nand_5 (nand_5_out, C, C);
  nand nand_6 (nand_6_out, A, A);
  nand nand_7 (nand_7_out, C, C);
  nand nand_8 (nand_8_out, A, A);
  nand nand_9 (nand_9_out, C, C);
  nand nand_10 (nand_10_out, B, B);
  nand nand_11 (nand_11_out, C, C);
  nand nand_12 (nand_12_out, B, B);
  nand nand_13 (nand_13_out, B, C);
  nand nand_14 (nand_14_out, A, A);
  nand nand_15 (nand_15_out, A, A);
  nand nand_16 (nand_16_out, B, B);
  nand nand_17 (nand_17_out, C, C);
  nand nand_18 (nand_18_out, B, B);
  nand nand_19 (nand_19_out, A, nand_1_out, C);
  nand nand_20 (nand_20_out, A, B, nand_2_out);
  nand nand_21 (nand_21_out, nand_3_out, nand_4_out);
  nand nand_22 (nand_22_out, B, nand_5_out);
  nand nand_23 (nand_23_out, nand_6_out, nand_7_out);
  nand nand_24 (nand_24_out, nand_8_out, B);
  nand nand_25 (nand_25_out, B, nand_9_out);
  nand nand_26 (nand_26_out, A, nand_10_out, C);
  nand nand_27 (nand_27_out, A, B, nand_11_out);
  nand nand_28 (nand_28_out, nand_12_out, C);
  nand nand_29 (nand_29_out, A, A);
  nand nand_30 (nand_30_out, nand_13_out, nand_14_out);
  nand nand_31 (nand_31_out, nand_15_out, nand_16_out, nand_17_out);
  nand nand_32 (nand_32_out, A, nand_18_out, C);
  nand nand_33 (nand_33_out, nand_19_out, nand_20_out);
  nand nand_34 (nand_34_out, nand_21_out, nand_22_out);
  nand nand_35 (nand_35_out, nand_23_out, nand_24_out, nand_25_out);
  nand nand_36 (nand_36_out, nand_26_out, nand_27_out);
  nand nand_37 (nand_37_out, nand_28_out, nand_29_out);
  nand nand_38 (f, nand_30_out, nand_30_out);
  nand nand_39 (nand_39_out, nand_31_out, nand_32_out);
  nand nand_40 (a_2, nand_33_out, nand_33_out);
  nand nand_41 (b_2, nand_34_out, nand_34_out);
  nand nand_42 (c_2, nand_35_out, nand_35_out);
  nand nand_43 (d, nand_36_out, nand_36_out);
  nand nand_44 (e, nand_37_out, nand_37_out);
  nand nand_45 (g, nand_39_out, nand_39_out);
endmodule

module Normal (
  input  A,
  input  B,
  input  C
);

  wire a_out, b_out, c_out, d_out, e_out, f_out, g_out, not_1_out, not_2_out, not_3_out, not_4_out,
       not_5_out, not_6_out, not_7_out, not_8_out, not_9_out, not_10_out, not_11_out, not_12_out, not_13_out,
       not_14_out, not_15_out, not_16_out, not_17_out, not_18_out, or_1_out, or_2_out, or_3_out, or_4_out,
       or_5_out, or_6_out, or_7_out, or_8_out, or_9_out, or_10_out, or_11_out, or_12_out, or_13_out;

  not not_1 (not_1_out, A);
  not not_2 (not_2_out, C);
  not not_3 (not_3_out, A);
  not not_4 (not_4_out, B);
  not not_5 (not_5_out, B);
  not not_6 (not_6_out, B);
  not not_7 (not_7_out, B);
  not not_8 (not_8_out, A);
  not not_9 (not_9_out, C);
  not not_10 (not_10_out, A);
  not not_11 (not_11_out, B);
  not not_12 (not_12_out, C);
  not not_13 (not_13_out, B);
  not not_14 (not_14_out, C);
  not not_15 (not_15_out, A);
  not not_16 (not_16_out, C);
  or or_1 (or_1_out, not_1_out, B, not_2_out);
  or or_2 (or_2_out, not_3_out, not_4_out, C);
  or or_3 (or_3_out, A, B);
  or or_4 (or_4_out, not_5_out, C);
  or or_5 (or_5_out, A, C);
  or or_6 (or_6_out, A, not_6_out);
  or or_7 (or_7_out, not_7_out, C);
  or or_8 (or_8_out, not_8_out, B, not_9_out);
  or or_9 (or_9_out, not_10_out, not_11_out, C);
  or or_10 (or_10_out, B, not_12_out);
  not not_17 (not_17_out, A);
  or or_11 (or_11_out, not_13_out, not_14_out);
  not not_18 (not_18_out, A);
  or or_12 (or_12_out, A, B, C);
  or or_13 (or_13_out, not_15_out, B, not_16_out);
  and u_a (a_out, or_1_out, or_2_out);
  and u_b (b_out, or_3_out, or_4_out);
  and u_c (c_out, or_5_out, or_6_out, or_7_out);
  and d (d_out, or_8_out, or_9_out);
  and e (e_out, or_10_out, not_17_out);
  and f (f_out, or_11_out, not_18_out);
  and g (g_out, or_12_out, or_13_out);
  _7_Segment_Display u_7_segment_display_1 (
    .g(g_out), .f(f_out), .a(a_out), .b(b_out), .e(e_out), .d(d_out), .c(c_out));  // open: dp
endmodule

module Universal (
  input  A,
  input  B,
  input  C
);

  wire a_out, b_out, c_out, d_out, e_out, f_out, g_out, nand_1_out, nand_2_out, nand_3_out, nand_4_out,
       nand_5_out, nand_6_out, nand_7_out, nand_8_out, nand_9_out, nand_10_out, nand_11_out, nand_12_out,
       nand_13_out, nand_14_out, nand_15_out, nand_16_out, nand_17_out, nand_18_out, nand_19_out,
       nand_20_out, nand_21_out, nand_22_out, nand_23_out, nand_24_out, nand_25_out, nand_26_out,
       nand_27_out, nand_28_out, nand_29_out, nand_30_out, nand_31_out, nand_32_out, nand_33_out,
       nand_34_out, nand_35_out, nand_36_out, nand_37_out, nand_38_out;

  nand nand_1 (nand_1_out, B, B);
  nand nand_2 (nand_2_out, C, C);
  nand nand_3 (nand_3_out, A, A);
  nand nand_4 (nand_4_out, B, B);
  nand nand_5 (nand_5_out, C, C);
  nand nand_6 (nand_6_out, A, A);
  nand nand_7 (nand_7_out, C, C);
  nand nand_8 (nand_8_out, A, A);
  nand nand_9 (nand_9_out, C, C);
  nand nand_10 (nand_10_out, B, B);
  nand nand_11 (nand_11_out, C, C);
  nand nand_12 (nand_12_out, B, B);
  nand nand_13 (nand_13_out, B, C);
  nand nand_14 (nand_14_out, A, A);
  nand nand_15 (nand_15_out, A, A);
  nand nand_16 (nand_16_out, B, B);
  nand nand_17 (nand_17_out, C, C);
  nand nand_18 (nand_18_out, B, B);
  nand nand_19 (nand_19_out, A, nand_1_out, C);
  nand nand_20 (nand_20_out, A, B, nand_2_out);
  nand nand_21 (nand_21_out, nand_3_out, nand_4_out);
  nand nand_22 (nand_22_out, B, nand_5_out);
  nand nand_23 (nand_23_out, nand_6_out, nand_7_out);
  nand nand_24 (nand_24_out, nand_8_out, B);
  nand nand_25 (nand_25_out, B, nand_9_out);
  nand nand_26 (nand_26_out, A, nand_10_out, C);
  nand nand_27 (nand_27_out, A, B, nand_11_out);
  nand nand_28 (nand_28_out, nand_12_out, C);
  nand nand_29 (nand_29_out, A, A);
  nand nand_30 (nand_30_out, nand_13_out, nand_14_out);
  nand nand_31 (nand_31_out, nand_15_out, nand_16_out, nand_17_out);
  nand nand_32 (nand_32_out, A, nand_18_out, C);
  nand nand_33 (nand_33_out, nand_19_out, nand_20_out);
  nand nand_34 (nand_34_out, nand_21_out, nand_22_out);
  nand nand_35 (nand_35_out, nand_23_out, nand_24_out, nand_25_out);
  nand nand_36 (nand_36_out, nand_26_out, nand_27_out);
  nand nand_37 (nand_37_out, nand_28_out, nand_29_out);
  nand f (f_out, nand_30_out, nand_30_out);
  nand nand_38 (nand_38_out, nand_31_out, nand_32_out);
  nand u_a (a_out, nand_33_out, nand_33_out);
  nand u_b (b_out, nand_34_out, nand_34_out);
  nand u_c (c_out, nand_35_out, nand_35_out);
  nand d (d_out, nand_36_out, nand_36_out);
  nand e (e_out, nand_37_out, nand_37_out);
  nand g (g_out, nand_38_out, nand_38_out);
  _7_Segment_Display u_7_segment_display_1 (
    .g(g_out), .f(f_out), .a(a_out), .b(b_out), .e(e_out), .d(d_out), .c(c_out));  // open: dp
endmodule

module Dcomb (
  input  A,
  input  B,
  input  C
);

  wire bcd27_1_a_2, bcd27_1_b_2, bcd27_1_c_2, bcd27_1_d, bcd27_1_e, bcd27_1_f, bcd27_1_g;

  BCD27 bcd27_1 (
    .A(A), .B(B), .C(C), .a_2(bcd27_1_a_2), .b_2(bcd27_1_b_2), .c_2(bcd27_1_c_2), .d(bcd27_1_d),
    .e(bcd27_1_e), .f(bcd27_1_f), .g(bcd27_1_g));
  _7_Segment_Display u_7_segment_display_1 (
    .g(bcd27_1_g), .f(bcd27_1_f), .a(bcd27_1_a_2), .b(bcd27_1_b_2), .e(bcd27_1_e), .d(bcd27_1_d),
    .c(bcd27_1_c_2));  // open: dp
endmodule

module mux (
  input  A,
  input  [1:0] S
);

  wire multiplexer_1_out, multiplexer_2_out, multiplexer_3_out, multiplexer_4_out, multiplexer_5_out,
       multiplexer_6_out, multiplexer_7_out, not_1_out;

  not not_1 (not_1_out, A);
  Multiplexer #(.select(2)) multiplexer_1 (
    .in0(1'b1), .in1(not_1_out), .in2(not_1_out), .in3(1'b1), .out(multiplexer_1_out), .sel(S));  // open: en
  Multiplexer #(.select(2)) multiplexer_2 (
    .in0(A), .in1(A), .in3(1'b1), .out(multiplexer_2_out), .sel(S));  // open: in2, en
  Multiplexer #(.select(2)) multiplexer_3 (
    .in0(A), .in1(1'b1), .in3(A), .out(multiplexer_3_out), .sel(S));  // open: in2, en
  Multiplexer #(.select(2)) multiplexer_4 (
    .in0(1'b1), .in1(not_1_out), .in2(not_1_out), .in3(1'b1), .out(multiplexer_4_out), .sel(S));  // open: en
  _7_Segment_Display u_7_segment_display_1 (
    .g(multiplexer_7_out), .f(multiplexer_6_out), .a(multiplexer_1_out), .b(multiplexer_2_out),
    .e(multiplexer_5_out), .d(multiplexer_4_out), .c(multiplexer_3_out));  // open: dp
  Multiplexer #(.select(2)) multiplexer_5 (
    .in0(not_1_out), .in2(not_1_out), .in3(not_1_out), .out(multiplexer_5_out), .sel(S));  // open: in1, en
  Multiplexer #(.select(2)) multiplexer_6 (
    .in0(not_1_out), .in1(not_1_out), .in2(not_1_out), .out(multiplexer_6_out), .sel(S));  // open: in3, en
  Multiplexer #(.select(2)) multiplexer_7 (
    .in0(A), .in1(not_1_out), .in2(1'b1), .in3(1'b1), .out(multiplexer_7_out), .sel(S));  // open: en

  // Notes on the sheet:
  //   a
  //   b
  //   c
  //   d
  //   e
  //   g f a b
  //   e d c h
  //   f
  //   g
endmodule
