// Logisim project LAB-2.1.circ as structural Verilog: 2 circuits, main circuit 1st Canonical Form Minterm
module _1st_Canonical_Form_Minterm (
  input  A,
  input  B,
  input  C
);

  wire and_1_out, and_2_out, and_3_out, not_1_out, not_2_out, not_3_out, or_1_out;

  not not_1 (not_1_out, A);
  not not_2 (not_2_out, B);
  not not_3 (not_3_out, C);
  and and_1 (and_1_out, not_1_out, not_2_out, C);
  and and_2 (and_2_out, A, B, not_3_out);
  and and_3 (and_3_out, not_1_out, B, not_3_out);
  or or_1 (or_1_out, and_1_out, and_3_out, and_2_out);
  LED led_1 (.in(or_1_out));

  // Notes on the sheet:
  //   C.1: 1st Canonical Form (Minterm)
endmodule

module _2nd_Canonical_Form_Maxterm (
  input  A,
  input  B,
  input  C
);

  wire and_1_out, and_2_out, not_1_out, not_2_out, not_3_out, or_1_out, or_2_out, or_3_out, or_4_out,
       or_5_out;

  not not_1 (not_1_out, B);
  not not_2 (not_2_out, A);
  not not_3 (not_3_out, C);
  or or_1 (or_1_out, A, B, C);
  or or_2 (or_2_out, A, not_1_out, not_3_out);
  or or_3 (or_3_out, not_2_out, B, C);
  and and_1 (and_1_out, or_1_out, or_2_out, or_3_out);
  or or_4 (or_4_out, not_2_out, B, not_3_out);
  or or_5 (or_5_out, not_2_out, not_1_out, not_3_out);
  and and_2 (and_2_out, and_1_out, or_4_out, or_5_out);
  LED led_1 (.in(and_2_out));

  // Notes on the sheet:
  //   C.1: 2nd Canonical Form (Maxterm)
  //   Tasnim Binte Rashid
  //   ID: 2121953642
endmodule
