// Logisim project LAB-3.circ as structural Verilog: 2 circuits, main circuit B2 NOR step-1
module B2_NOR_step_1 (
  input  A,
  input  B,
  input  C
);

  wire nor_1_out, nor_2_out, nor_3_out, nor_4_out, nor_5_out, nor_6_out, nor_7_out;

  nor nor_1 (nor_1_out, A, A);
  nor nor_2 (nor_2_out, B, B);
  nor nor_3 (nor_3_out, C, C);
  nor nor_4 (nor_4_out, nor_1_out, nor_3_out);
  nor nor_5 (nor_5_out, nor_2_out, C);
  nor nor_6 (nor_6_out, nor_4_out, nor_5_out);
  nor nor_7 (nor_7_out, nor_6_out, nor_6_out);
  LED led_1 (.in(nor_7_out));

  // Notes on the sheet:
  //   B2 .1:  AC+BC' with NOR gate
  //   Muhtadina Serniabat Tasin
  //   ID: 2232160642
endmodule

module B2_NOR_step_2 (
  input  A,
  input  B,
  input  C
);

  wire nor_1_out, nor_2_out, nor_3_out, nor_4_out, nor_5_out, nor_6_out, nor_7_out;

  nor nor_1 (nor_1_out, A, A);
  nor nor_2 (nor_2_out, B, B);
  nor nor_3 (nor_3_out, C, C);
  nor nor_4 (nor_4_out, A, B);
  nor nor_5 (nor_5_out, B, C);
  nor nor_6 (nor_6_out, A, nor_3_out);
  nor nor_7 (nor_7_out, nor_4_out, nor_6_out, nor_5_out);
  LED led_1 (.in(nor_7_out));

  // Notes on the sheet:
  //   B2 .2:  AC+BC' with NOR gate
  //   Muhtadina Serniabat Tasin
  //   ID: 2232160642
endmodule
