// Logisim project LAB-4.circ as structural Verilog: 1 circuit, main circuit main
module main (
  input  w,
  input  x,
  input  y,
  input  z
);

  wire and_1_out, and_2_out, and_3_out, and_4_out, and_5_out, and_6_out, and_7_out, not_1_out, not_2_out,
       not_3_out, or_1_out, or_2_out, or_3_out;

  not not_1 (not_1_out, x);
  not not_2 (not_2_out, y);
  not not_3 (not_3_out, z);
  and and_1 (and_1_out, x, y);
  and and_2 (and_2_out, x, z);
  and and_3 (and_3_out, not_1_out, y);
  and and_4 (and_4_out, not_1_out, z);
  and and_5 (and_5_out, x, not_2_out, not_3_out);
  and and_6 (and_6_out, not_2_out, not_3_out);
  and and_7 (and_7_out, y, z);
  or or_1 (or_1_out, w, and_1_out, and_2_out);
  or or_2 (or_2_out, and_3_out, and_4_out, and_5_out);
  or or_3 (or_3_out, and_6_out, and_7_out);
  LED A (.in(or_1_out));
  LED B (.in(or_2_out));
  LED C (.in(or_3_out));
  LED D (.in(not_3_out));

  // Notes on the sheet:
  //   Fig: BCD to Excess-3 Converter
  //   Tasnim Binte Rashid
  //   2121953642
endmodule
