// Logisim project LAB-5.circ as structural Verilog: 1 circuit, main circuit main
module main (
  input  A0,
  input  B0,
  input  Carry_in,
  input  A1,
  input  B1,
  input  A2,
  input  B2,
  input  A3,
  input  B3,
  output [3:0] Sum,
  output Carry_Out
);

  wire and_1_out, and_2_out, and_3_out, and_4_out, and_5_out, and_6_out, and_7_out, and_8_out, or_1_out,
       or_2_out, or_3_out, xor_1_out, xor_2_out, xor_3_out, xor_4_out;

  xor xor_1 (xor_1_out, A0, B0);
  xor xor_2 (xor_2_out, A1, B1);
  xor xor_3 (xor_3_out, A2, B2);
  xor xor_4 (xor_4_out, A3, B3);
  xor xor_5 (Sum[0], xor_1_out, Carry_in);
  and and_1 (and_1_out, Carry_in, xor_1_out);
  or or_1 (or_1_out, and_1_out, and_2_out);
  and and_2 (and_2_out, A0, B0);
  xor xor_6 (Sum[1], xor_2_out, or_1_out);
  and and_3 (and_3_out, or_1_out, xor_2_out);
  or or_2 (or_2_out, and_3_out, and_4_out);
  and and_4 (and_4_out, A1, B1);
  xor xor_7 (Sum[2], xor_3_out, or_2_out);
  and and_5 (and_5_out, or_2_out, xor_3_out);
  or or_3 (or_3_out, and_5_out, and_6_out);
  and and_6 (and_6_out, A2, B2);
  xor xor_8 (Sum[3], xor_4_out, or_3_out);
  and and_7 (and_7_out, or_3_out, xor_4_out);
  or or_4 (Carry_Out, and_7_out, and_8_out);
  and and_8 (and_8_out, A3, B3);

  // Notes on the sheet:
  //   Fig: BCD Adder
  //   A = 1001 = 9
  //   B = 0000 = 0
  //   A + B = 9 + 0 = 9 = Sum = 1001
  //   Carry Out = 0
  //   Tasnim Binte Rashid
  //   ID: 2121953642
endmodule
