// Logisim project LAB-6.circ as structural Verilog: 3 circuits, main circuit main
module main (
  input  D,
  input  C,
  input  B,
  input  A
);

  wire n7447_1_a_2, n7447_1_b_2, n7447_1_c_2, n7447_1_d_2, n7447_1_e, n7447_1_f, n7447_1_g;

  _7447 u_7447_1 (
    .D(D), .C(C), .B(B), .A(A), .c_2(n7447_1_c_2), .a_2(n7447_1_a_2), .b_2(n7447_1_b_2), .d_2(n7447_1_d_2),
    .e(n7447_1_e), .f(n7447_1_f), .g(n7447_1_g));
  _7_Segment_Display u_7_segment_display_1 (
    .g(n7447_1_g), .f(n7447_1_f), .a(n7447_1_c_2), .b(n7447_1_a_2), .e(n7447_1_e), .d(n7447_1_d_2),
    .c(n7447_1_b_2));  // open: dp

  // Notes on the sheet:
  //   Muhtadina Serniabat Tasin
  //   2232160642
  //   Mou Deshmukh
  //   2022274642
  //   Fig: BCD to 7 Segment Decoder Implementation
  //   Jukta Bhowmik
  //   2031341042
  //   Tasnim Binte Rashid
  //   2121953642
endmodule

module _7447 (
  input  D,
  input  C,
  input  B,
  input  A,
  output c_2,
  output a_2,
  output b_2,
  output d_2,
  output e,
  output f,
  output g
);

  wire and_1_out, and_2_out, and_3_out, and_4_out, and_5_out, and_6_out, and_7_out, and_8_out, and_9_out,
       and_10_out, and_11_out, and_12_out, and_13_out, and_14_out, and_15_out, and_16_out, not_1_out,
       not_2_out, not_3_out, not_4_out, not_5_out, not_6_out, not_7_out, not_8_out, not_9_out, not_10_out,
       not_11_out, not_12_out, not_13_out, not_14_out, not_15_out, not_16_out, not_17_out, not_18_out,
       not_19_out, not_20_out, not_21_out;

  not not_1 (not_1_out, C);
  and and_1 (and_1_out, not_1_out, not_2_out);
  not not_2 (not_2_out, A);
  and and_2 (and_2_out, C, A);
  not not_3 (not_3_out, C);
  not not_4 (not_4_out, B);
  and and_3 (and_3_out, not_4_out, not_5_out);
  not not_5 (not_5_out, A);
  and and_4 (and_4_out, B, A);
  or or_1 (a_2, and_1_out, B, and_2_out, D);
  or or_2 (b_2, not_3_out, and_3_out, and_4_out);
  not not_6 (not_6_out, B);
  not not_7 (not_7_out, C);
  not not_8 (not_8_out, A);
  not not_9 (not_9_out, C);
  not not_10 (not_10_out, A);
  not not_11 (not_11_out, B);
  not not_12 (not_12_out, C);
  not not_13 (not_13_out, A);
  not not_14 (not_14_out, A);
  not not_15 (not_15_out, B);
  not not_16 (not_16_out, A);
  not not_17 (not_17_out, B);
  not not_18 (not_18_out, A);
  not not_19 (not_19_out, C);
  not not_20 (not_20_out, B);
  not not_21 (not_21_out, A);
  or or_3 (c_2, not_6_out, A, C);
  and and_5 (and_5_out, not_7_out, not_8_out);
  and and_6 (and_6_out, not_9_out, B);
  and and_7 (and_7_out, B, not_10_out);
  and and_8 (and_8_out, C, not_11_out, A);
  and and_9 (and_9_out, not_12_out, not_13_out);
  and and_10 (and_10_out, B, not_14_out);
  and and_11 (and_11_out, not_15_out, not_16_out);
  and and_12 (and_12_out, C, not_17_out);
  and and_13 (and_13_out, C, not_18_out);
  and and_14 (and_14_out, not_19_out, B);
  and and_15 (and_15_out, C, not_20_out);
  and and_16 (and_16_out, C, not_21_out);
  or or_4 (d_2, and_5_out, and_6_out, and_7_out, and_8_out, D);
  or or_5 (e, and_9_out, and_10_out);
  or or_6 (f, and_11_out, and_12_out, and_13_out, D);
  or or_7 (g, and_14_out, and_15_out, and_16_out, D);

  // Notes on the sheet:
  //   Tasnim Binte Rashid
  //   2121953642
  //   Mou Deshmukh
  //   2022274642
  //   Muhtadina Serniabat Tasin
  //   2232160642
  //   Fig: BCD to 7 Segment Decoder Circuit
  //   Jukta Bhowmik
  //   2031341042
endmodule

module nand_decoder (
  input  D,
  input  C,
  input  B,
  input  A,
  output b_2,
  output e,
  output a_2,
  output c_2,
  output f,
  output d_2,
  output g
);

  wire nand_1_out, nand_2_out, nand_3_out, nand_4_out, nand_5_out, nand_6_out, nand_8_out, nand_9_out,
       nand_10_out, nand_11_out, nand_12_out, nand_13_out, nand_14_out, nand_15_out, nand_16_out,
       nand_17_out, nand_18_out, nand_20_out, nand_21_out, nand_22_out, nand_23_out, nand_24_out,
       nand_27_out, nand_28_out, nand_29_out, nand_30_out, nand_31_out, nand_32_out, nand_33_out,
       nand_34_out, nand_35_out, nand_36_out, nand_37_out, nand_38_out, nand_39_out, nand_40_out,
       nand_41_out, nand_42_out, nand_43_out, nand_44_out, nand_45_out, nand_46_out;

  nand nand_1 (nand_1_out, C, C);
  nand nand_2 (nand_2_out, A, A);
  nand nand_3 (nand_3_out, nand_1_out, nand_2_out);
  nand nand_4 (nand_4_out, B, B);
  nand nand_5 (nand_5_out, C, A);
  nand nand_6 (nand_6_out, C, C);
  nand nand_7 (a_2, nand_3_out, nand_4_out, nand_5_out, nand_6_out);
  nand nand_8 (nand_8_out, B, B);
  nand nand_9 (nand_9_out, A, A);
  nand nand_10 (nand_10_out, A, A);
  nand nand_11 (nand_11_out, C, C);
  nand nand_12 (nand_12_out, C, C);
  nand nand_13 (nand_13_out, A, A);
  nand nand_14 (nand_14_out, C, C);
  nand nand_15 (nand_15_out, A, A);
  nand nand_16 (nand_16_out, B, B);
  nand nand_17 (nand_17_out, nand_8_out, nand_9_out);
  nand nand_18 (nand_18_out, B, A);
  nand nand_19 (c_2, B, nand_10_out, nand_11_out);
  nand nand_20 (nand_20_out, nand_12_out, nand_13_out);
  nand nand_21 (nand_21_out, nand_14_out, B);
  nand nand_22 (nand_22_out, B, nand_15_out);
  nand nand_23 (nand_23_out, C, nand_16_out, A);
  nand nand_24 (nand_24_out, C, C);
  nand nand_25 (b_2, C, nand_17_out, nand_18_out);
  nand nand_26 (d_2, nand_20_out, nand_21_out, nand_22_out, nand_23_out, nand_24_out);
  nand nand_27 (nand_27_out, C, C);
  nand nand_28 (nand_28_out, A, A);
  nand nand_29 (nand_29_out, A, A);
  nand nand_30 (nand_30_out, B, B);
  nand nand_31 (nand_31_out, A, A);
  nand nand_32 (nand_32_out, B, B);
  nand nand_33 (nand_33_out, A, A);
  nand nand_34 (nand_34_out, C, C);
  nand nand_35 (nand_35_out, B, B);
  nand nand_36 (nand_36_out, A, A);
  nand nand_37 (nand_37_out, nand_27_out, nand_28_out);
  nand nand_38 (nand_38_out, B, nand_29_out);
  nand nand_39 (nand_39_out, nand_30_out, nand_31_out);
  nand nand_40 (nand_40_out, C, nand_32_out);
  nand nand_41 (nand_41_out, C, nand_33_out);
  nand nand_42 (nand_42_out, C, C);
  nand nand_43 (nand_43_out, nand_34_out, B);
  nand nand_44 (nand_44_out, C, nand_35_out);
  nand nand_45 (nand_45_out, C, nand_36_out);
  nand nand_46 (nand_46_out, C, C);
  nand nand_47 (e, nand_37_out, nand_38_out);
  nand nand_48 (f, nand_39_out, nand_40_out, nand_41_out, nand_42_out);
  nand nand_49 (g, nand_43_out, nand_44_out, nand_45_out, nand_46_out);

  assign D = C;

  // Notes on the sheet:
  //   Muhtadina Serniabat Tasin
  //   2232160642
  //   Fig: BCD to 7 Segment Decoder Circuit
  //   Tasnim Binte Rashid
  //   2121953642
  //   Jukta Bhowmik
  //   2031341042
  //   Mou Deshmukh
  //   2022274642
endmodule
