// Logisim project LAB-7.circ as structural Verilog: 1 circuit, main circuit main
module main (
  input  A,
  input  B,
  input  C,
  input  _1,
  input  _0
);

  wire and_1_out, and_2_out, and_3_out, and_4_out, not_1_out, not_2_out, not_3_out, or_1_out, or_2_out,
       or_3_out;

  not not_1 (not_1_out, A);
  not not_2 (not_2_out, B);
  not not_3 (not_3_out, C);
  and and_1 (and_1_out, not_1_out, not_2_out, not_3_out);
  and and_2 (and_2_out, C, _1, not_2_out);
  and and_3 (and_3_out, B, _0, not_3_out);
  and and_4 (and_4_out, A, B, C);
  or or_1 (or_1_out, and_1_out, and_2_out);
  or or_2 (or_2_out, and_3_out, and_4_out);
  or or_3 (or_3_out, or_1_out, or_2_out);
  LED led_1 (.in(or_3_out));

  // Notes on the sheet:
  //   LAB-7: 4*1 Multiplexer
  //   Muhtadina Serniabat Tasin
  //   2232160642
  //   Mou Deshmukh
  //   2022274642
  //   Tasnim Binte Rashid
  //   2121953642
  //   Jukta Bhowmik
  //   2031341042
endmodule
